// Logisim project ProjetoUnidade2.circ as structural Verilog: 8 circuits, main circuit testeULA
module HalfAdder (
  input  A,
  input  B,
  output S,
  output Co
);

  xor xor_1 (S, A, B);
  and and_1 (Co, A, B);
endmodule

module FullAdder (
  input  Ci,
  input  A,
  input  B,
  output S,
  output Co
);

  wire halfadder_1_co, halfadder_1_s, halfadder_2_co;

  HalfAdder halfadder_1 (.A(A), .B(B), .S(halfadder_1_s), .Co(halfadder_1_co));
  HalfAdder halfadder_2 (.A(Ci), .B(halfadder_1_s), .S(S), .Co(halfadder_2_co));
  or or_1 (Co, halfadder_2_co, halfadder_1_co);
endmodule

module Somador4Bits (
  input  Cin,
  input  A0,
  input  B0,
  input  A1,
  input  B1,
  input  A2,
  input  B2,
  input  A3,
  input  B3,
  output S0,
  output S1,
  output S2,
  output S3,
  output Co
);

  wire fulladder_1_co, fulladder_2_co, fulladder_3_co;

  FullAdder fulladder_1 (.Ci(Cin), .A(A0), .B(B0), .S(S0), .Co(fulladder_1_co));
  FullAdder fulladder_2 (.Ci(fulladder_1_co), .A(A1), .B(B1), .S(S1), .Co(fulladder_2_co));
  FullAdder fulladder_3 (.Ci(fulladder_2_co), .A(A2), .B(B2), .S(S2), .Co(fulladder_3_co));
  FullAdder fulladder_4 (.Ci(fulladder_3_co), .A(A3), .B(B3), .S(S3), .Co(Co));
endmodule

module Somador8Bits (
  input  Cin,
  input  A0,
  input  B0,
  input  A1,
  input  B1,
  input  A2,
  input  B2,
  input  A3,
  input  B3,
  input  A4,
  input  B4,
  input  A5,
  input  B5,
  input  A6,
  input  B6,
  input  A7,
  input  B7,
  output S0,
  output S1,
  output S2,
  output S3,
  output S4,
  output S5,
  output S6,
  output S7,
  output Co
);

  wire somador4bits_1_co;

  Somador4Bits somador4bits_1 (
    .Cin(Cin), .A0(A0), .B0(B0), .A1(A1), .B1(B1), .A2(A2), .B2(B2), .A3(A3), .B3(B3), .S0(S0), .S1(S1),
    .S2(S2), .S3(S3), .Co(somador4bits_1_co));
  Somador4Bits somador4bits_2 (
    .Cin(somador4bits_1_co), .A0(A4), .B0(B4), .A1(A5), .B1(B5), .A2(A6), .B2(B6), .A3(A7), .B3(B7), .S0(S4),
    .S1(S5), .S2(S6), .S3(S7), .Co(Co));
endmodule

module ULA (
  input  [7:0] A,
  input  [7:0] B,
  input  S2,
  input  S1,
  input  S0,
  output [7:0] F
);

  wire operacao_nand_1_p17, somador8bits_1_co, subtrador8bits_1_t8;
  wire [7:0] operacao_and_1_s0, operacao_nand_1_p19, operacao_nor_1_s0, operacao_or_1_s0, operacao_xnor_1_s0,
       operacao_xor_1_s0, somador8bits_1_s0, subtrador8bits_1_s0;

  subtrador8bits subtrador8bits_1 (
    .t0(1'b0), .A0(A[0]), .B0(B[0]), .A1(A[1]), .B1(B[1]), .A2(A[2]), .B2(B[2]), .A3(A[3]), .B3(B[3]),
    .A4(A[4]), .B4(B[4]), .A5(A[5]), .B5(B[5]), .A6(A[6]), .B6(B[6]), .A7(A[7]), .B7(B[7]),
    .S0(subtrador8bits_1_s0[0]), .S1(subtrador8bits_1_s0[1]), .S2(subtrador8bits_1_s0[2]),
    .S3(subtrador8bits_1_s0[3]), .S4(subtrador8bits_1_s0[4]), .S5(subtrador8bits_1_s0[5]),
    .S6(subtrador8bits_1_s0[6]), .S7(subtrador8bits_1_s0[7]), .t8(subtrador8bits_1_t8));
  operacao_or operacao_or_1 (
    .A0(A[0]), .A1(A[1]), .A2(A[2]), .A3(A[3]), .A4(A[4]), .A5(A[5]), .A6(A[6]), .A7(A[7]), .B0(B[0]),
    .B1(B[1]), .B2(B[2]), .B3(B[3]), .B4(B[4]), .B5(B[5]), .B6(B[6]), .B7(B[7]), .S0(operacao_or_1_s0[0]),
    .S1(operacao_or_1_s0[1]), .S2(operacao_or_1_s0[2]), .S3(operacao_or_1_s0[3]), .S4(operacao_or_1_s0[4]),
    .S5(operacao_or_1_s0[5]), .S6(operacao_or_1_s0[6]), .S7(operacao_or_1_s0[7]));
  // operacao_nand operacao_nand_1: pin names not known; wires that end beside it: A[0], A[1], A[2], A[3], A[4], A[5], A[6], A[7], B[0], B[1], B[2], B[3], B[4], B[5], B[6], B[7], operacao_nand_1_p17, operacao_nand_1_p17, operacao_nand_1_p19[0], operacao_nand_1_p19[1], operacao_nand_1_p19[2], operacao_nand_1_p19[3], operacao_nand_1_p19[4], operacao_nand_1_p19[5], operacao_nand_1_p19[6], operacao_nand_1_p19[7]
  operacao_and operacao_and_1 (
    .A0(A[0]), .A1(A[1]), .A2(A[2]), .A3(A[3]), .A4(A[4]), .A5(A[5]), .A6(A[6]), .A7(A[7]), .B0(B[0]),
    .B1(B[1]), .B2(B[2]), .B3(B[3]), .B4(B[4]), .B5(B[5]), .B6(B[6]), .B7(B[7]), .S0(operacao_and_1_s0[0]),
    .S1(operacao_and_1_s0[1]), .S2(operacao_and_1_s0[2]), .S3(operacao_and_1_s0[3]),
    .S4(operacao_and_1_s0[4]), .S5(operacao_and_1_s0[5]), .S6(operacao_and_1_s0[6]), .S7(operacao_and_1_s0[7]));
  operacao_xor operacao_xor_1 (
    .A0(A[0]), .A1(A[1]), .A2(A[2]), .A3(A[3]), .A4(A[4]), .A5(A[5]), .A6(A[6]), .A7(A[7]), .B0(B[0]),
    .B1(B[1]), .B2(B[2]), .B3(B[3]), .B4(B[4]), .B5(B[5]), .B6(B[6]), .B7(B[7]), .S0(operacao_xor_1_s0[0]),
    .S1(operacao_xor_1_s0[1]), .S2(operacao_xor_1_s0[2]), .S3(operacao_xor_1_s0[3]),
    .S4(operacao_xor_1_s0[4]), .S5(operacao_xor_1_s0[5]), .S6(operacao_xor_1_s0[6]), .S7(operacao_xor_1_s0[7]));
  operacao_xnor operacao_xnor_1 (
    .A0(A[0]), .A1(A[1]), .A2(A[2]), .A3(A[3]), .A4(A[4]), .A5(A[5]), .A6(A[6]), .A7(A[7]), .B0(B[0]),
    .B1(B[1]), .B2(B[2]), .B3(B[3]), .B4(B[4]), .B5(B[5]), .B6(B[6]), .B7(B[7]), .S0(operacao_xnor_1_s0[0]),
    .out_18(operacao_xnor_1_s0[1]), .out_19(operacao_xnor_1_s0[2]), .out_20(operacao_xnor_1_s0[3]),
    .out_21(operacao_xnor_1_s0[4]), .out_22(operacao_xnor_1_s0[5]), .out_23(operacao_xnor_1_s0[6]),
    .out_24(operacao_xnor_1_s0[7]));
  Somador8Bits somador8bits_1 (
    .Cin(1'b0), .A0(A[0]), .B0(B[0]), .A1(A[1]), .B1(B[1]), .A2(A[2]), .B2(B[2]), .A3(A[3]), .B3(B[3]),
    .A4(A[4]), .B4(B[4]), .A5(A[5]), .B5(B[5]), .A6(A[6]), .B6(B[6]), .A7(A[7]), .B7(B[7]),
    .S0(somador8bits_1_s0[0]), .S1(somador8bits_1_s0[1]), .S2(somador8bits_1_s0[2]),
    .S3(somador8bits_1_s0[3]), .S4(somador8bits_1_s0[4]), .S5(somador8bits_1_s0[5]),
    .S6(somador8bits_1_s0[6]), .S7(somador8bits_1_s0[7]), .Co(somador8bits_1_co));
  operacao_nor operacao_nor_1 (
    .A0(A[0]), .A1(A[1]), .A2(A[2]), .A3(A[3]), .A4(A[4]), .A5(A[5]), .A6(A[6]), .A7(A[7]), .B0(B[0]),
    .B1(B[1]), .B2(B[2]), .B3(B[3]), .B4(B[4]), .B5(B[5]), .B6(B[6]), .B7(B[7]), .S0(operacao_nor_1_s0[0]),
    .S1(operacao_nor_1_s0[1]), .S2(operacao_nor_1_s0[2]), .S3(operacao_nor_1_s0[3]),
    .S4(operacao_nor_1_s0[4]), .S5(operacao_nor_1_s0[5]), .S6(operacao_nor_1_s0[6]), .S7(operacao_nor_1_s0[7]));
  MUXcom8bits muxcom8bits_1 (
    .Soma(somador8bits_1_s0), .Sub(subtrador8bits_1_s0), .OpAND(operacao_and_1_s0), .OpOR(operacao_or_1_s0),
    .OpXOR(operacao_xor_1_s0), .OpNAND(operacao_nand_1_p19), .OpNOR(operacao_nor_1_s0),
    .OpXNOR(operacao_xnor_1_s0), .S2(S2), .S1(S1), .S0(S0), .F0(F[0]), .F1(F[1]), .F2(F[2]), .F3(F[3]),
    .F4(F[4]), .F5(F[5]), .F6(F[6]), .F7(F[7]));
endmodule

module MUX8x1 (
  input  Soma,
  input  Sub,
  input  OpAND,
  input  OpOR,
  input  OpXOR,
  input  OpNAND,
  input  OpNOR,
  input  OpXNOR,
  input  S2,
  input  S1,
  input  S0,
  output F
);

  wire and_1_out, and_2_out, and_3_out, and_4_out, and_5_out, and_6_out, and_7_out, and_8_out;

  and and_1 (and_1_out, Soma, ~S2, ~S1, ~S0);  // AND_Gate
  and and_2 (and_2_out, Sub, ~S2, ~S1, S0);  // AND_Gate
  and and_3 (and_3_out, OpAND, ~S2, S1, ~S0);  // AND_Gate
  and and_4 (and_4_out, OpOR, ~S2, S1, S0);  // AND_Gate
  and and_5 (and_5_out, OpXOR, S2, ~S1, ~S0);  // AND_Gate
  and and_6 (and_6_out, OpNAND, S2, ~S1, S0);  // AND_Gate
  and and_7 (and_7_out, OpNOR, S2, S1, ~S0);  // AND_Gate
  and and_8 (and_8_out, OpXNOR, S2, S1, S0);
  or or_1 (F, and_1_out, and_2_out, and_3_out, and_4_out, and_5_out, and_6_out, and_7_out, and_8_out);
endmodule

module MUXcom8bits (
  input  [7:0] Soma,
  input  [7:0] Sub,
  input  [7:0] OpAND,
  input  [7:0] OpOR,
  input  [7:0] OpXOR,
  input  [7:0] OpNAND,
  input  [7:0] OpNOR,
  input  [7:0] OpXNOR,
  input  S2,
  input  S1,
  input  S0,
  output F0,
  output F1,
  output F2,
  output F3,
  output F4,
  output F5,
  output F6,
  output F7
);

  MUX8x1 mux8x1_1 (
    .Soma(Soma[0]), .Sub(Sub[0]), .OpAND(OpAND[0]), .OpOR(OpOR[0]), .OpXOR(OpXOR[0]), .OpNAND(OpNAND[0]),
    .OpNOR(OpNOR[0]), .OpXNOR(OpXNOR[0]), .S2(S2), .S1(S1), .S0(S0), .F(F0));
  MUX8x1 mux8x1_2 (
    .Soma(Soma[1]), .Sub(Sub[1]), .OpAND(OpAND[1]), .OpOR(OpOR[1]), .OpXOR(OpXOR[1]), .OpNAND(OpNAND[1]),
    .OpNOR(OpNOR[1]), .OpXNOR(OpXNOR[1]), .S2(S2), .S1(S1), .S0(S0), .F(F1));
  MUX8x1 mux8x1_3 (
    .Soma(Soma[2]), .Sub(Sub[2]), .OpAND(OpAND[2]), .OpOR(OpOR[2]), .OpXOR(OpXOR[2]), .OpNAND(OpNAND[2]),
    .OpNOR(OpNOR[2]), .OpXNOR(OpXNOR[2]), .S2(S2), .S1(S1), .S0(S0), .F(F2));
  MUX8x1 mux8x1_4 (
    .Soma(Soma[3]), .Sub(Sub[3]), .OpAND(OpAND[3]), .OpOR(OpOR[3]), .OpXOR(OpXOR[3]), .OpNAND(OpNAND[3]),
    .OpNOR(OpNOR[3]), .OpXNOR(OpXNOR[3]), .S2(S2), .S1(S1), .S0(S0), .F(F3));
  MUX8x1 mux8x1_5 (
    .Soma(Soma[4]), .Sub(Sub[4]), .OpAND(OpAND[4]), .OpOR(OpOR[4]), .OpXOR(OpXOR[4]), .OpNAND(OpNAND[4]),
    .OpNOR(OpNOR[4]), .OpXNOR(OpXNOR[4]), .S2(S2), .S1(S1), .S0(S0), .F(F4));
  MUX8x1 mux8x1_6 (
    .Soma(Soma[5]), .Sub(Sub[5]), .OpAND(OpAND[5]), .OpOR(OpOR[5]), .OpXOR(OpXOR[5]), .OpNAND(OpNAND[5]),
    .OpNOR(OpNOR[5]), .OpXNOR(OpXNOR[5]), .S2(S2), .S1(S1), .S0(S0), .F(F5));
  MUX8x1 mux8x1_7 (
    .Soma(Soma[6]), .Sub(Sub[6]), .OpAND(OpAND[6]), .OpOR(OpOR[6]), .OpXOR(OpXOR[6]), .OpNAND(OpNAND[6]),
    .OpNOR(OpNOR[6]), .OpXNOR(OpXNOR[6]), .S2(S2), .S1(S1), .S0(S0), .F(F6));
  MUX8x1 mux8x1_8 (
    .Soma(Soma[7]), .Sub(Sub[7]), .OpAND(OpAND[7]), .OpOR(OpOR[7]), .OpXOR(OpXOR[7]), .OpNAND(OpNAND[7]),
    .OpNOR(OpNOR[7]), .OpXNOR(OpXNOR[7]), .S2(S2), .S1(S1), .S0(S0), .F(F7));
endmodule

module testeULA (
  input  [7:0] A,
  input  [7:0] B,
  input  in_3,
  input  in_4,
  input  in_5,
  output [7:0] out_6
);

  ULA ula_1 (.A(A), .B(B), .S2(in_3), .S1(in_4), .S0(in_5), .F(out_6));
endmodule
