// Logisim project operacoes_logicas.circ as structural Verilog: 6 circuits, main circuit operacao_and
module operacao_and (
  input  A0,
  input  A1,
  input  A2,
  input  A3,
  input  A4,
  input  A5,
  input  A6,
  input  A7,
  input  B0,
  input  B1,
  input  B2,
  input  B3,
  input  B4,
  input  B5,
  input  B6,
  input  B7,
  output S0,
  output S1,
  output S2,
  output S3,
  output S4,
  output S5,
  output S6,
  output S7
);

  and and_1 (S0, A0, B0);
  and and_2 (S1, A1, B1);
  and and_3 (S2, A2, B2);
  and and_4 (S3, A3, B3);
  and and_5 (S4, A4, B4);
  and and_6 (S5, A5, B5);
  and and_7 (S6, A6, B6);
  and and_8 (S7, A7, B7);
endmodule

module operacao_or (
  input  A0,
  input  A1,
  input  A2,
  input  A3,
  input  A4,
  input  A5,
  input  A6,
  input  A7,
  input  B0,
  input  B1,
  input  B2,
  input  B3,
  input  B4,
  input  B5,
  input  B6,
  input  B7,
  output S0,
  output S1,
  output S2,
  output S3,
  output S4,
  output S5,
  output S6,
  output S7
);

  or or_1 (S0, A0, B0);
  or or_2 (S1, A1, B1);
  or or_3 (S2, A2, B2);
  or or_4 (S3, A3, B3);
  or or_5 (S4, A4, B4);
  or or_6 (S5, A5, B5);
  or or_7 (S6, A6, B6);
  or or_8 (S7, A7, B7);
endmodule

module operacao_xor (
  input  A0,
  input  A1,
  input  A2,
  input  A3,
  input  A4,
  input  A5,
  input  A6,
  input  A7,
  input  B0,
  input  B1,
  input  B2,
  input  B3,
  input  B4,
  input  B5,
  input  B6,
  input  B7,
  output S0,
  output S1,
  output S2,
  output S3,
  output S4,
  output S5,
  output S6,
  output S7
);

  xor xor_1 (S0, A0, B0);
  xor xor_2 (S1, A1, B1);
  xor xor_3 (S2, A2, B2);
  xor xor_4 (S3, A3, B3);
  xor xor_5 (S4, A4, B4);
  xor xor_6 (S5, A5, B5);
  xor xor_7 (S6, A6, B6);
  xor xor_8 (S7, A7, B7);
endmodule

module operacao_nand (
  input  A0,
  input  A1,
  input  A2,
  input  A3,
  input  A4,
  input  A5,
  input  A6,
  input  A7,
  input  B0,
  input  B1,
  input  B2,
  input  B3,
  input  B4,
  input  B5,
  input  B6,
  input  B7,
  output S0,
  output S1,
  output S2,
  output S3,
  output S4,
  output S5,
  output S6,
  output S7
);

  nand nand_1 (S0, A0, B0);
  nand nand_2 (S1, A1, B1);
  nand nand_3 (S2, A2, B2);
  nand nand_4 (S3, A3, B3);
  nand nand_5 (S4, A4, B4);
  nand nand_6 (S5, A5, B5);
  nand nand_7 (S6, A6, B6);
  nand nand_8 (S7, A7, B7);
endmodule

module operacao_nor (
  input  A0,
  input  A1,
  input  A2,
  input  A3,
  input  A4,
  input  A5,
  input  A6,
  input  A7,
  input  B0,
  input  B1,
  input  B2,
  input  B3,
  input  B4,
  input  B5,
  input  B6,
  input  B7,
  output S0,
  output S1,
  output S2,
  output S3,
  output S4,
  output S5,
  output S6,
  output S7
);

  nor nor_1 (S0, A0, B0);
  nor nor_2 (S1, A1, B1);
  nor nor_3 (S2, A2, B2);
  nor nor_4 (S3, A3, B3);
  nor nor_5 (S4, A4, B4);
  nor nor_6 (S5, A5, B5);
  nor nor_7 (S6, A6, B6);
  nor nor_8 (S7, A7, B7);
endmodule

module operacao_xnor (
  input  A0,
  input  A1,
  input  A2,
  input  A3,
  input  A4,
  input  A5,
  input  A6,
  input  A7,
  input  B0,
  input  B1,
  input  B2,
  input  B3,
  input  B4,
  input  B5,
  input  B6,
  input  B7,
  output S0,
  output out_18,
  output out_19,
  output out_20,
  output out_21,
  output out_22,
  output out_23,
  output out_24
);

  wire xor_1_out, xor_2_out, xor_3_out, xor_4_out, xor_5_out, xor_6_out, xor_7_out, xor_8_out;

  xor xor_1 (xor_1_out, A0, B0);
  xor xor_2 (xor_2_out, A1, B1);
  xor xor_3 (xor_3_out, A2, B2);
  xor xor_4 (xor_4_out, A3, B3);
  xor xor_5 (xor_5_out, A4, B4);
  xor xor_6 (xor_6_out, A5, B5);
  xor xor_7 (xor_7_out, A6, B6);
  xor xor_8 (xor_8_out, A7, B7);
  not not_1 (S0, xor_1_out);
  not not_2 (out_18, xor_2_out);
  not not_3 (out_19, xor_3_out);
  not not_4 (out_20, xor_4_out);
  not not_5 (out_21, xor_5_out);
  not not_6 (out_22, xor_6_out);
  not not_7 (out_23, xor_7_out);
  not not_8 (out_24, xor_8_out);
endmodule
