// Logisim project subtrador.circ as structural Verilog: 4 circuits, main circuit halfsubtactor
module halfsubtactor (
  input  A,
  input  B,
  output S,
  output t0
);

  wire not_1_out;

  not not_1 (not_1_out, A);
  xor xor_1 (S, A, B);
  and and_1 (t0, not_1_out, B);
endmodule

module full_subtractor (
  input  ti,
  input  A,
  input  B,
  output S,
  output t0
);

  wire and_1_out, and_2_out, and_3_out, not_1_out, xor_1_out;

  not not_1 (not_1_out, A);
  and and_1 (and_1_out, not_1_out, B);
  and and_2 (and_2_out, B, ti);
  and and_3 (and_3_out, not_1_out, ti);
  xor xor_1 (xor_1_out, A, B);
  xor xor_2 (S, xor_1_out, ti);
  or or_1 (t0, and_1_out, and_2_out, and_3_out);
endmodule

module subtrador4bits (
  input  t0,
  input  A0,
  input  B0,
  input  A1,
  input  B1,
  input  A2,
  input  B2,
  input  A3,
  input  B3,
  output S0,
  output S1,
  output S2,
  output S3,
  output t4
);

  wire full_subtractor_1_t0, full_subtractor_2_t0, full_subtractor_3_t0;

  full_subtractor full_subtractor_1 (.ti(t0), .A(A0), .B(B0), .S(S0), .t0(full_subtractor_1_t0));
  full_subtractor full_subtractor_2 (.ti(full_subtractor_1_t0), .A(A1), .B(B1), .S(S1), .t0(full_subtractor_2_t0));
  full_subtractor full_subtractor_3 (.ti(full_subtractor_2_t0), .A(A2), .B(B2), .S(S2), .t0(full_subtractor_3_t0));
  full_subtractor full_subtractor_4 (.ti(full_subtractor_3_t0), .A(A3), .B(B3), .S(S3), .t0(t4));
endmodule

module subtrador8bits (
  input  t0,
  input  A0,
  input  B0,
  input  A1,
  input  B1,
  input  A2,
  input  B2,
  input  A3,
  input  B3,
  input  A4,
  input  B4,
  input  A5,
  input  B5,
  input  A6,
  input  B6,
  input  A7,
  input  B7,
  output S0,
  output S1,
  output S2,
  output S3,
  output S4,
  output S5,
  output S6,
  output S7,
  output t8
);

  wire subtrador4bits_1_t4;

  subtrador4bits subtrador4bits_1 (
    .t0(t0), .A0(A0), .B0(B0), .A1(A1), .B1(B1), .A2(A2), .B2(B2), .A3(A3), .B3(B3), .S0(S0), .S1(S1),
    .S2(S2), .S3(S3), .t4(subtrador4bits_1_t4));
  subtrador4bits subtrador4bits_2 (
    .t0(subtrador4bits_1_t4), .A0(A4), .B0(B4), .A1(A5), .B1(B5), .A2(A6), .B2(B6), .A3(A7), .B3(B7),
    .S0(S4), .S1(S5), .S2(S6), .S3(S7), .t4(t8));
endmodule
